// Logisim project test.circ as structural Verilog: 1 circuit, main circuit main
module main (
);

  wire adder_1_cout, and_1_out, button_1_out, clock_1_out, counter_2_carry, decoder_1_out0, decoder_1_out1,
       decoder_1_out2, decoder_1_out3, decoder_1_out4, decoder_1_out5, decoder_1_out6, decoder_1_out7,
       not_1_out, not_2_out, or_1_out, or_2_out, pull_resistor_1_node, pull_resistor_2_node,
       pull_resistor_4_node, pull_resistor_5_node, pull_resistor_6_node, pull_resistor_8_node,
       subtractor_1_bout, transistor_1_out, transistor_7_out;
  wire [1:0] not_3_out;
  wire [2:0] register_3_q;
  wire [3:0] Address_q, Address_q_2, counter_2_q, counter_2_q_2, transistor_2_out, transistor_2_out_2;
  wire [7:0] A_q, adder_1_out, and_2_out, B_q, or_3_out, ram_1_data, register_2_q, register_4_q,
       register_5_q, register_6_q, register_7_q, register_8_q, register_9_q, register_10_q, register_11_q,
       rom_1_data, subtractor_1_out, SWAP_q, transistor_10_out, transistor_11_out;
  wire [7:6] Befehl_q;
  wire [7:7] pull_resistor_14_node;
  wire [11:0] counter_1_q;
  wire [11:8] counter_3_q, register_1_q;
  wire [23:0] rom_2_data;

  // Probe on {register_1_q, Address_q_2, Address_q}
  Register #(.width(4)) register_1 (
    .D(counter_3_q), .en(rom_2_data[12]), .Q(register_1_q), .clk(transistor_1_out), .clr(button_1_out));
  Pull_Resistor #(.pull(1)) pull_resistor_1 (.node(pull_resistor_1_node));
  Clock clock_1 (.out(clock_1_out));
  Button button_1 (.out(button_1_out));
  ROM #(.addrWidth(12)) rom_1 (
    .addr({register_1_q, Address_q_2, Address_q}), .data(rom_1_data), .sel(pull_resistor_1_node));
  Pull_Resistor pull_resistor_2 (.node(pull_resistor_2_node));
  DotMatrix #(.inputtype("row"), .matrixcols(24), .matrixrows(1)) dotmatrix_1 (.row0(rom_2_data));
  Transistor #(.\type ("n")) transistor_1 (.in(clock_1_out), .out(transistor_1_out), .gate(not_1_out));
  Pull_Resistor pull_resistor_3 (.node(transistor_1_out));
  Transistor #(.\type ("n"), .width(8)) transistor_2 (
    .in(rom_1_data), .out({transistor_2_out_2, transistor_2_out}), .gate(rom_2_data[13]));
  or or_1 (or_1_out, button_1_out, pull_resistor_2_node);
  // Probe on counter_1_q
  Pull_Resistor #(.pull(1)) pull_resistor_4 (.node(pull_resistor_4_node));
  not not_1 (not_1_out, rom_2_data[14]);
  Register Address (
    .D({transistor_2_out_2, transistor_2_out}), .en(rom_2_data[12]), .Q({Address_q_2, Address_q}),
    .clk(transistor_1_out), .clr(button_1_out));
  Pull_Resistor #(.pull(1)) pull_resistor_5 (.node(pull_resistor_5_node));
  Counter #(.width(4), .max('hf)) counter_1 (
    .count(pull_resistor_6_node), .Q(counter_1_q[3:0]), .clk(transistor_1_out), .clr(or_1_out));  // open: load, D, carry
  Pull_Resistor #(.pull(1)) pull_resistor_6 (.node(pull_resistor_6_node));
  ROM #(.addrWidth(12), .dataWidth(24)) rom_2 (.addr(counter_1_q), .data(rom_2_data), .sel(pull_resistor_4_node));
  // Probe on register_2_q
  Register register_2 (
    .D({transistor_2_out_2, transistor_2_out}), .en(rom_2_data[11]), .Q(register_2_q),
    .clk(transistor_1_out), .clr(button_1_out));
  RAM #(.bus("separate")) ram_1 (
    .addr({Address_q_2, Address_q}), .din({transistor_2_out_2, transistor_2_out}), .data(ram_1_data),
    .str(rom_2_data[1]), .sel(pull_resistor_5_node), .clk(transistor_1_out), .ld(pull_resistor_5_node));  // open: clr
  Register Befehl (
    .D({transistor_2_out_2, transistor_2_out}), .en(rom_2_data[7]), .Q({Befehl_q, counter_1_q[9:4]}),
    .clk(transistor_1_out), .clr(button_1_out));
  DotMatrix #(.inputtype("row"), .matrixcols(8), .matrixrows(1), .dotshape("circle")) dotmatrix_2 (.row0({transistor_2_out_2, transistor_2_out}));
  Pull_Resistor pull_resistor_7 (.node({transistor_2_out_2, transistor_2_out}));
  Transistor #(.\type ("n"), .width(8)) transistor_3 (
    .in(ram_1_data), .out({transistor_2_out_2, transistor_2_out}), .gate(rom_2_data[8]));
  Register #(.width(3)) register_3 (
    .D(transistor_2_out[2:0]), .en(rom_2_data[18]), .Q(register_3_q), .clk(transistor_1_out),
    .clr(button_1_out));
  Decoder #(.select(3)) decoder_1 (
    .out0(decoder_1_out0), .out1(decoder_1_out1), .out2(decoder_1_out2), .out3(decoder_1_out3),
    .out4(decoder_1_out4), .out5(decoder_1_out5), .out6(decoder_1_out6), .out7(decoder_1_out7),
    .sel(register_3_q), .en(rom_2_data[17]));
  and and_1 (and_1_out, counter_2_carry, rom_2_data[4]);
  Counter counter_2 (
    .load(rom_2_data[6]), .D({transistor_2_out_2, transistor_2_out}), .count(rom_2_data[4]),
    .Q({counter_2_q_2, counter_2_q}), .carry(counter_2_carry), .clk(transistor_1_out), .clr(button_1_out));
  Register A (
    .D({transistor_2_out_2, transistor_2_out}), .en(rom_2_data[2]), .Q(A_q), .clk(transistor_1_out),
    .clr(button_1_out));
  Register B (
    .D({transistor_2_out_2, transistor_2_out}), .en(rom_2_data[0]), .Q(B_q), .clk(transistor_1_out),
    .clr(button_1_out));
  Register SWAP (
    .D({transistor_2_out_2, transistor_2_out}), .en(rom_2_data[23]), .Q(SWAP_q), .clk(transistor_1_out),
    .clr(button_1_out));
  Pull_Resistor pull_resistor_8 (.node(pull_resistor_8_node));
  Pull_Resistor pull_resistor_9 (.node(decoder_1_out0));
  DotMatrix #(.inputtype("row"), .matrixcols(12), .matrixrows(1), .dotshape("circle")) dotmatrix_3 (.row0({counter_3_q, counter_2_q_2, counter_2_q}));
  Counter #(.width(4), .max('hf)) counter_3 (
    .load(rom_2_data[15]), .D(transistor_2_out), .count(and_1_out), .Q(counter_3_q), .clk(transistor_1_out),
    .clr(button_1_out));  // open: carry
  Transistor #(.\type ("n"), .width(8)) transistor_4 (
    .in(A_q), .out({transistor_2_out_2, transistor_2_out}), .gate(rom_2_data[3]));
  Transistor #(.\type ("n"), .width(8)) transistor_5 (
    .in(B_q), .out({transistor_2_out_2, transistor_2_out}), .gate(rom_2_data[16]));
  Transistor #(.\type ("n"), .width(8)) transistor_6 (
    .in(SWAP_q), .out({transistor_2_out_2, transistor_2_out}), .gate(rom_2_data[22]));
  Transistor #(.\type ("n")) transistor_7 (.in(subtractor_1_bout), .out(transistor_7_out), .gate(rom_2_data[9]));
  Transistor #(.\type ("n")) transistor_8 (.in(adder_1_cout), .out(pull_resistor_8_node), .gate(not_2_out));
  Register register_4 (
    .D({transistor_2_out_2, transistor_2_out}), .en(decoder_1_out0), .Q(register_4_q),
    .clk(transistor_1_out), .clr(button_1_out));
  Register register_5 (
    .D({transistor_2_out_2, transistor_2_out}), .en(decoder_1_out1), .Q(register_5_q),
    .clk(transistor_1_out), .clr(button_1_out));
  Pull_Resistor pull_resistor_10 (.node(decoder_1_out1));
  Transistor #(.\type ("n"), .width(8)) transistor_9 (
    .in({counter_2_q_2, counter_2_q}), .out({transistor_2_out_2, transistor_2_out}), .gate(rom_2_data[5]));
  Pull_Resistor pull_resistor_11 (.node(transistor_7_out));
  or or_2 (or_2_out, transistor_7_out, pull_resistor_8_node);
  Register register_6 (
    .D({transistor_2_out_2, transistor_2_out}), .en(decoder_1_out2), .Q(register_6_q),
    .clk(transistor_1_out), .clr(button_1_out));
  Register register_7 (
    .D({transistor_2_out_2, transistor_2_out}), .en(decoder_1_out3), .Q(register_7_q),
    .clk(transistor_1_out), .clr(button_1_out));
  Pull_Resistor pull_resistor_12 (.node(decoder_1_out2));
  Pull_Resistor pull_resistor_13 (.node(decoder_1_out3));
  Pull_Resistor pull_resistor_14 (.node(pull_resistor_14_node[7]));
  assign or_3_out = A_q | B_q;  // OR_Gate or_3, 8 bits wide
  assign and_2_out = A_q & B_q;  // AND_Gate and_2, 8 bits wide
  Adder adder_1 (.a(A_q), .b(B_q), .out(adder_1_out), .cout(adder_1_cout));  // open: cin
  Transistor #(.\type ("n"), .width(8)) transistor_10 (.in(adder_1_out), .out(transistor_10_out), .gate(not_2_out));
  not not_2 (not_2_out, rom_2_data[9]);
  Subtractor subtractor_1 (.a(A_q), .b(B_q), .out(subtractor_1_out), .bout(subtractor_1_bout));  // open: bin
  Transistor #(.\type ("n"), .width(8)) transistor_11 (
    .in(subtractor_1_out), .out(transistor_11_out), .gate(rom_2_data[10]));
  DotMatrix #(.inputtype("row"), .matrixcols(2), .matrixrows(1), .dotshape("circle")) dotmatrix_4 (.row0(counter_1_q[11:10]));
  Register #(.width(2)) Flags (
    .D(not_3_out), .en(rom_2_data[10]), .Q(counter_1_q[11:10]), .clk(transistor_1_out), .clr(button_1_out));
  Register register_8 (
    .D({transistor_2_out_2, transistor_2_out}), .en(decoder_1_out4), .Q(register_8_q),
    .clk(transistor_1_out), .clr(button_1_out));
  Register register_9 (
    .D({transistor_2_out_2, transistor_2_out}), .en(decoder_1_out5), .Q(register_9_q),
    .clk(transistor_1_out), .clr(button_1_out));
  Pull_Resistor pull_resistor_15 (.node(decoder_1_out4));
  Pull_Resistor pull_resistor_16 (.node(decoder_1_out5));
  Transistor #(.\type ("n"), .width(8)) transistor_12 (
    .in({pull_resistor_14_node[7], A_q[7:1]}), .out({transistor_2_out_2, transistor_2_out}),
    .gate(rom_2_data[21]));
  Transistor #(.\type ("n"), .width(8)) transistor_13 (
    .in(or_3_out), .out({transistor_2_out_2, transistor_2_out}), .gate(rom_2_data[20]));
  Transistor #(.\type ("n"), .width(8)) transistor_14 (
    .in(and_2_out), .out({transistor_2_out_2, transistor_2_out}), .gate(rom_2_data[19]));
  Transistor #(.\type ("n"), .width(8)) transistor_15 (
    .in(transistor_10_out), .out({transistor_2_out_2, transistor_2_out}), .gate(rom_2_data[10]));
  Transistor #(.\type ("n"), .width(8)) transistor_16 (
    .in(transistor_11_out), .out({transistor_2_out_2, transistor_2_out}), .gate(rom_2_data[9]));
  not not_3 (not_3_out[0], or_2_out);
  Register register_10 (
    .D({transistor_2_out_2, transistor_2_out}), .en(decoder_1_out6), .Q(register_10_q),
    .clk(transistor_1_out), .clr(button_1_out));
  Register register_11 (
    .D({transistor_2_out_2, transistor_2_out}), .en(decoder_1_out7), .Q(register_11_q),
    .clk(transistor_1_out), .clr(button_1_out));
  Pull_Resistor pull_resistor_17 (.node(decoder_1_out7));
  Pull_Resistor pull_resistor_18 (.node(decoder_1_out6));
  DotMatrix #(.inputtype("row"), .matrixcols(8), .matrixrows(8), .dotshape("circle")) dotmatrix_5 (
    .row0(register_4_q), .row1(register_5_q), .row2(register_6_q), .row3(register_7_q), .row4(register_8_q),
    .row5(register_9_q), .row6(register_10_q), .row7(register_11_q));
  or or_4 (not_3_out[1], transistor_2_out[0], transistor_2_out[1], transistor_2_out[2], transistor_2_out[3], transistor_2_out_2[0], transistor_2_out_2[1], transistor_2_out_2[2], transistor_2_out_2[3]);

  // Notes on the sheet:
  //   Program
  //   contents of rom_1 (hex, n*v repeats v):
  //   10 0 81 11 81 80 10 40 81 11 80 82 6 81 82 13 18 0 10 1 82 12 1b 0 10 0 82 c 82 3 0 14 40 0 11 80 81
  //   5 0 81 10 0 83 11 83 82 17 82 81 10 1 82 11 80 83 4 82 83 11 83 80 12 6 0 10 1 83 11 83 82 5 0 82 10
  //   1 84 11 84 83 17 83 82 10 a 84 11 84 83 5 0 83 10 1 85 11 85 84 17 84 83 10 10 85 11 85 84 5 0 84 10
  //   1 86 11 86 85 17 85 84 10 11 86 11 86 85 5 0 85 10 1 87 11 87 86 17 86 85 10 12 87 11 87 86 5 0 86
  //   10 1 88 11 88 87 17 87 86 10 0 88 11 88 87 10 0 89 11 89 88 10 8 89 11 88 8a 6 89 8a 13 b8 0 10 1 8a
  //   12 bb 0 10 0 8a c 8a 3 0 14 3b 1 10 0 8b 11 8b 8a 10 8 8b 11 8a 8c 6 8b 8c 13 da 0 10 1 8c 12 dd 0
  //   10 0 8c c 8c 3 0 14 23 1 11 89 8b 4 89 8b 11 8b 89 11 87 8b 5 0 8b 16 8b c 8b 3 0 14 8 1 10 1 8b 11
  //   89 8c 4 8b 8c 11 8c 89 10 1 8b 11 87 8c 4 8b 8c 11 8c 87 10 1 8b 11 8a 8c 4 8b 8c 11 8c 8a 12 c8 0
  //   11 88 8b 11 89 8c 15 8b 8c 10 1 8b 11 88 8c 4 8b 8c 11 8c 88 12 a6 0 10 1 8b c 8b 3 0 14 83 4 10 0
  //   8b 11 8b 87 10 0 8c 11 8c 8b 10 8 8c 11 8b 8d 6 8c 8d 13 63 1 10 1 8d 12 66 1 10 0 8d c 8d 3 0 14 cb
  //   3 10 0 8d 11 8d 8c 10 8 8d 11 8c 8e 6 8d 8e 13 85 1 10 1 8e 12 88 1 10 0 8e c 8e 3 0 14 bc 3 11 87
  //   8d c 8d 1 11 87 8d 10 0 8f 11 8f 8e 10 0 90 11 90 8f 10 3 90 11 8f 91 6 90 91 13 b6 1 10 1 91 12 b9
  //   1 10 0 91 c 91 3 0 14 1c 3 10 1 91 11 8f 92 6 91 92 11 8b 91 4 92 91 11 91 90 10 0 91 11 8b 92 6 91
  //   92 14 e4 1 10 0 92 12 e7 1 10 1 92 c 92 3 0 14 fa 1 10 8 91 11 90 92 4 91 92 11 92 90 10 7 91 11 8b
  //   92 6 91 92 14 c 2 10 0 92 12 f 2 10 1 92 c 92 3 0 14 22 2 10 8 91 11 90 92 6 91 92 11 92 90 10 0 92
  //   11 92 91 10 3 92 11 91 93 6 92 93 13 3a 2 10 1 93 12 3d 2 10 0 93 c 93 3 0 14 d 3 10 1 93 11 91 94 6
  //   93 94 11 8c 93 4 94 93 11 93 92 10 0 93 11 8c 94 6 93 94 14 68 2 10 0 94 12 6b 2 10 1 94 c 94 3 0 14
  //   7e 2 10 8 93 11 92 94 4 93 94 11 94 92 10 7 93 11 8c 94 6 93 94 14 90 2 10 0 94 12 93 2 10 1 94 c 94
  //   3 0 14 a6 2 10 8 93 11 92 94 6 93 94 11 94 92 11 92 93 10 0 95 11 95 94 10 8 95 11 94 96 6 95 96 13
  //   c1 2 10 1 96 12 c4 2 10 0 96 c 96 3 0 14 e3 2 11 93 95 4 90 95 11 95 93 10 1 95 11 94 96 4 95 96 11
  //   96 94 12 af 2 11 93 95 5 0 95 16 95 c 95 3 0 14 fe 2 10 1 95 11 8e 96 4 95 96 11 96 8e 10 1 95 11 91
  //   96 4 95 96 11 96 91 12 28 2 10 1 95 11 8f 96 4 95 96 11 96 8f 12 a4 1 11 87 95 5 0 95 16 95 c 95 3 0
  //   14 37 3 10 1 95 11 8e 96 6 95 96 11 96 8e 11 87 95 5 40 95 10 0 97 11 97 96 17 96 95 10 3 96 11 8e
  //   97 6 96 97 14 58 3 10 0 97 12 5b 3 10 1 97 c 97 3 0 14 71 3 11 87 96 5 40 96 10 1 98 11 98 97 17 97
  //   96 10 2 97 11 8e 98 6 97 98 14 83 3 10 0 98 12 86 3 10 1 98 c 98 3 0 14 a1 3 11 87 97 5 40 97 11 87
  //   99 5 0 99 16 99 11 99 98 17 98 97 10 1 98 11 87 99 4 98 99 11 99 87 10 1 98 11 8c 99 4 98 99 11 99
  //   8c 12 73 1 10 1 98 11 8b 99 4 98 99 11 99 8b 12 51 1 10 0 98 11 98 87 10 0 99 11 99 98 10 8 99 11 98
  //   9a 6 99 9a 13 e9 3 10 1 9a 12 ec 3 10 0 9a c 9a 3 0 14 80 4 10 0 9b 11 9b 9a 10 8 9b 11 9a 9c 6 9b
  //   9c 13 b 4 10 1 9c 12 e 4 10 0 9c c 9c 3 0 14 68 4 11 99 9b 4 99 9b 11 9b 99 11 87 9b 5 0 9b 16 9b c
  //   9b 3 0 14 39 4 10 1 9b 11 99 9c 4 9b 9c 11 9c 99 11 87 9b 5 0 9b 11 87 9d 5 40 9d 16 9d 11 9d 9c 17
  //   9c 9b 10 1 9c 11 87 9d 4 9c 9d 11 9d 87 10 1 9c 11 9a 9d 4 9c 9d 11 9d 9a 12 f9 3 11 98 9c 11 99 9d
  //   15 9c 9d 10 1 9c 11 98 9d 4 9c 9d 11 9d 98 12 d7 3 12 3b 1
  //   Microcode
  //   RAM
  //   contents of rom_2 (hex, n*v repeats v):
  //   1020 2090 4000 13*0 1020 2090 808 13*0 1020 2090 1020 3010 101 404 10*0 1020 2090 1020 2011 404 11*0
  //   1020 2090 1020 3010 101 1020 3010 104 402 7*0 1020 2090 1020 2011 1020 3010 104 402 8*0 1020 2090
  //   1020 3010 101 1020 3010 104 602 7*0 1020 2090 1020 2011 1020 3010 104 602 8*0 1020 2090 1020 3010
  //   101 1020 3010 104 80002 7*0 1020 2090 1020 3010 101 1020 3010 104 100002 7*0 1020 2090 1020 3010 104
  //   200002 10*0 1020 2090 1020 3010 a 11*0 1020 2090 1020 3010 104 11*0 1020 2090 1020 2014 12*0 1020
  //   2090 1020 3010 10002 11*0 1020 2090 1020 3010 101 11*0 1020 2090 1020 802010 1020 3010 400002 9*0
  //   1020 2090 1020 3010 800100 1020 3010 400002 8*0 1020 2090 1020 802010 1020 a000 400040 9*0 1020 2090
  //   10 10 12*0 1020 2090 1020 802010 1020 a000 400040 9*0 1020 2090 1020 3010 40100 1020 3010 20100 8*0
  //   1020 2090 1020 3000 1100 800100 1020 3010 400002 7*0 1020 2090 1020 3010 800100 1020 3010 1100
  //   400002 7*0 1020 2090 1020 3010 1100 800100 1020 3010 400002 7*0 1020 2090 14*0 1020 2090 14*0 1020
  //   2090 14*0 1020 2090 14*0 1020 2090 14*0 1020 2090 14*0 1020 2090 14*0 1020 2090 14*0 1020 2090 14*0
  //   1020 2090 14*0 1020 2090 14*0 1020 2090 14*0 1020 2090 14*0 1020 2090 14*0 1020 2090 14*0 1020 2090
  //   14*0 1020 2090 14*0 1020 2090 14*0 1020 2090 14*0 1020 2090 14*0 1020 2090 14*0 1020 2090 14*0 1020
  //   2090 14*0 1020 2090 14*0 1020 2090 14*0 1020 2090 14*0 1020 2090 14*0 1020 2090 14*0 1020 2090 14*0
  //   1020 2090 14*0 1020 2090 14*0 1020 2090 14*0 1020 2090 14*0 1020 2090 14*0 1020 2090 14*0 1020 2090
  //   14*0 1020 2090 14*0 1020 2090 14*0 1020 2090 14*0 1020 2090 4000 13*0 1020 2090 808 13*0 1020 2090
  //   1020 3010 101 404 10*0 1020 2090 1020 2011 404 11*0 1020 2090 1020 3010 101 1020 3010 104 402 7*0
  //   1020 2090 1020 2011 1020 3010 104 402 8*0 1020 2090 1020 3010 101 1020 3010 104 602 7*0 1020 2090
  //   1020 2011 1020 3010 104 602 8*0 1020 2090 1020 3010 101 1020 3010 104 80002 7*0 1020 2090 1020 3010
  //   101 1020 3010 104 100002 7*0 1020 2090 1020 3010 104 200002 10*0 1020 2090 1020 3010 a 11*0 1020
  //   2090 1020 3010 104 11*0 1020 2090 1020 2014 12*0 1020 2090 1020 3010 10002 11*0 1020 2090 1020 3010
  //   101 11*0 1020 2090 1020 802010 1020 3010 400002 9*0 1020 2090 1020 3010 800100 1020 3010 400002 8*0
  //   1020 2090 1020 802010 1020 a000 400040 9*0 1020 2090 1020 802010 1020 a000 400040 9*0 1020 2090 1020
  //   802010 1020 a000 400040 9*0 1020 2090 1020 3010 40100 1020 3010 20100 8*0 1020 2090 1020 3000 1100
  //   800100 1020 3010 400002 7*0 1020 2090 1020 3010 800100 1020 3010 1100 400002 7*0 1020 2090 1020 3010
  //   1100 800100 1020 3010 400002 7*0 1020 2090 14*0 1020 2090 14*0 1020 2090 14*0 1020 2090 14*0 1020
  //   2090 14*0 1020 2090 14*0 1020 2090 14*0 1020 2090 14*0 1020 2090 14*0 1020 2090 14*0 1020 2090 14*0
  //   1020 2090 14*0 1020 2090 14*0 1020 2090 14*0 1020 2090 14*0 1020 2090 14*0 1020 2090 14*0 1020 2090
  //   14*0 1020 2090 14*0 1020 2090 14*0 1020 2090 14*0 1020 2090 14*0 1020 2090 14*0 1020 2090 14*0 1020
  //   2090 14*0 1020 2090 14*0 1020 2090 14*0 1020 2090 14*0 1020 2090 14*0 1020 2090 14*0 1020 2090 14*0
  //   1020 2090 14*0 1020 2090 14*0 1020 2090 14*0 1020 2090 14*0 1020 2090 14*0 1020 2090 14*0 1020 2090
  //   14*0 1020 2090 14*0 1020 2090 4000 13*0 1020 2090 808 13*0 1020 2090 1020 3010 101 404 10*0 1020
  //   2090 1020 2011 404 11*0 1020 2090 1020 3010 101 1020 3010 104 402 7*0 1020 2090 1020 2011 1020 3010
  //   104 402 8*0 1020 2090 1020 3010 101 1020 3010 104 602 7*0 1020 2090 1020 2011 1020 3010 104 602 8*0
  //   1020 2090 1020 3010 101 1020 3010 104 80002 7*0 1020 2090 1020 3010 101 1020 3010 104 100002 7*0
  //   1020 2090 1020 3010 104 200002 10*0 1020 2090 1020 3010 a 11*0 1020 2090 1020 3010 104 11*0 1020
  //   2090 1020 2014 12*0 1020 2090 1020 3010 10002 11*0 1020 2090 1020 3010 101 11*0 1020 2090 1020
  //   802010 1020 3010 400002 9*0 1020 2090 1020 3010 800100 1020 3010 400002 8*0 1020 2090 1020 802010
  //   1020 a000 400040 9*0 1020 2090 10 10 12*0 1020 2090 10 10 12*0 1020 2090 1020 3010 40100 1020 3010
  //   20100 8*0 1020 2090 1020 3000 1100 800100 1020 3010 400002 7*0 1020 2090 1020 3010 800100 1020 3010
  //   1100 400002 7*0 1020 2090 1020 3010 1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
endmodule
